// Logisim project main.circ as structural Verilog: 1 circuit, main circuit main
module main (
);

  wire Clock;
  wire [7:0] INT_BITFIELD;
  wire [8:0] INT_COUNTER;
  wire [15:0] INT_ARG1, INT_ARG2;

  Clock clock_1 (.out(Clock));
  ROM #(.addrWidth(9), .dataWidth(40)) PROG (.addr(INT_COUNTER), .data({INT_ARG2, INT_ARG1, INT_BITFIELD}));
  Counter #(.max('h1ff), .width(9)) counter_1 (.clk(Clock), .Q(INT_COUNTER));  // open: clr, load, up, count, D, carry

  // Other names for the same wires on the sheet: INT_OPCODE[7:0] = INT_BITFIELD;
  //   INT_BITFIELD[39:8] = {INT_ARG2, INT_ARG1}

  // Notes on the sheet:
  //   contents of PROG (hex, n*v repeats v):
  //   55405640 66546645 5aa5ffff a00
endmodule
